// Logisim project project.circ as structural Verilog: 9 circuits, main circuit main
module main (
);

  wire clk, select_out, set, stop;
  wire [3:0] bcd_1_big_digit, bcd_1_small_digit, bcd_2_big_digit, bcd_2_small_digit, joystick_1_x,
       joystick_1_y;
  wire [7:0] cell_x, cell_y, joystick, some_cdm8e_1_adr;
  wire [15:0] displ_module_1__1st_row, displ_module_1__2nd_row, displ_module_1__3rd_row,
       displ_module_1__4th_row, displ_module_1__5th_row, displ_module_1__6th_row, displ_module_1__7th_row,
       displ_module_1__8th_row, displ_module_1__9th_row, displ_module_1__10th_row, displ_module_1__11th_row,
       displ_module_1__12th_row, displ_module_1__13th_row, displ_module_1__14th_row,
       displ_module_1__15th_row, displ_module_1__16th_row, game_1_halted, game_1_halted_2, game_1_halted_3,
       game_1_halted_4, game_1_halted_5, game_1_halted_6, game_1_halted_7, game_1_halted_8, game_1_halted_9,
       game_1_halted_10, game_1_halted_11, game_1_halted_12, game_1_halted_13, game_1_halted_14,
       game_1_halted_15, game_1_halted_16;

  Clock clock_1 (.out(clk));
  Button select (.out(select_out));
  some_cdm8e some_cdm8e_1 (.adr(some_cdm8e_1_adr), .clk(clk), .joystick(joystick), .cell_x(cell_x), .cell_y(cell_y));
  Button u_set (.out(set));
  T_Flip_Flop t_ff_1 (.clk(select_out), .T(select_out), .Q(stop));  // open: Qn, preset, reset, en
  Joystick joystick_1 (.x(joystick_1_x), .y(joystick_1_y));
  // Probe on some_cdm8e_1_adr
  Hex_Digit_Display hex_digit_display_1 (.value(bcd_1_big_digit));  // open: dp
  Hex_Digit_Display hex_digit_display_2 (.value(bcd_1_small_digit));  // open: dp
  bcd bcd_1 (.\input (cell_y), .big_digit(bcd_1_big_digit), .small_digit(bcd_1_small_digit));
  // Probe on joystick_1_x
  joystick_parse joystick_parse_1 (.in_1(joystick_1_x), .in_2(joystick_1_y), .\output (joystick));
  // Probe on joystick_1_y
  game game_1 (
    .clk(clk), .adr(some_cdm8e_1_adr), .set(set), .halted(game_1_halted), .halted_2(game_1_halted_2),
    .halted_3(game_1_halted_3), .halted_4(game_1_halted_4), .halted_5(game_1_halted_5),
    .halted_6(game_1_halted_6), .halted_7(game_1_halted_7), .halted_8(game_1_halted_8),
    .halted_9(game_1_halted_9), .halted_10(game_1_halted_10), .halted_11(game_1_halted_11),
    .halted_12(game_1_halted_12), .halted_13(game_1_halted_13), .halted_14(game_1_halted_14),
    .halted_15(game_1_halted_15), .halted_16(game_1_halted_16), .stop(stop));  // open: cell_out
  Hex_Digit_Display hex_digit_display_3 (.value(bcd_2_small_digit));  // open: dp
  Hex_Digit_Display hex_digit_display_4 (.value(bcd_2_big_digit));  // open: dp
  bcd bcd_2 (.\input (cell_x), .big_digit(bcd_2_big_digit), .small_digit(bcd_2_small_digit));
  // Probe on joystick
  DotMatrix #(.inputtype("row"), .matrixcols(16), .matrixrows(16)) dotmatrix_1 (
    .row0(game_1_halted), .row1(game_1_halted_2), .row2(game_1_halted_3), .row3(game_1_halted_4),
    .row4(game_1_halted_5), .row5(game_1_halted_6), .row6(game_1_halted_7), .row7(game_1_halted_8),
    .row8(game_1_halted_9), .row9(game_1_halted_10), .row10(game_1_halted_11), .row11(game_1_halted_12),
    .row12(game_1_halted_13), .row13(game_1_halted_14), .row14(game_1_halted_15), .row15(game_1_halted_16));
  DotMatrix #(.inputtype("row"), .matrixcols(16), .matrixrows(16)) dotmatrix_2 (
    .row0(displ_module_1__1st_row), .row1(displ_module_1__2nd_row), .row2(displ_module_1__3rd_row),
    .row3(displ_module_1__4th_row), .row4(displ_module_1__5th_row), .row5(displ_module_1__6th_row),
    .row6(displ_module_1__7th_row), .row7(displ_module_1__8th_row), .row8(displ_module_1__9th_row),
    .row9(displ_module_1__10th_row), .row10(displ_module_1__11th_row), .row11(displ_module_1__12th_row),
    .row12(displ_module_1__13th_row), .row13(displ_module_1__14th_row), .row14(displ_module_1__15th_row),
    .row15(displ_module_1__16th_row));
  displ_module displ_module_1 (
    ._1st_row(displ_module_1__1st_row), ._2nd_row(displ_module_1__2nd_row),
    ._3rd_row(displ_module_1__3rd_row), ._4th_row(displ_module_1__4th_row),
    ._5th_row(displ_module_1__5th_row), ._6th_row(displ_module_1__6th_row),
    ._7th_row(displ_module_1__7th_row), ._8th_row(displ_module_1__8th_row),
    ._9th_row(displ_module_1__9th_row), ._10th_row(displ_module_1__10th_row),
    ._11th_row(displ_module_1__11th_row), ._12th_row(displ_module_1__12th_row),
    ._13th_row(displ_module_1__13th_row), ._14th_row(displ_module_1__14th_row),
    ._15th_row(displ_module_1__15th_row), ._16th_row(displ_module_1__16th_row));  // open: lo, set_Lo, hi, sel_Hi, adr, sel_adr, clk

  // Notes on the sheet:
  //   up-down
endmodule

// jstk_prs
module joystick_parse (
  input  [3:0] in_1,
  input  [3:0] in_2,
  output [7:0] \output 
);

  Comparator #(.width(4), .mode("unsigned")) comparator_1 (.a(in_1), .b(4'b0101), .lt(\output [0]));  // open: gt, eq
  Comparator #(.width(4), .mode("unsigned")) comparator_2 (.a(in_1), .b(4'b1010), .gt(\output [1]));  // open: eq, lt
  Comparator #(.width(4), .mode("unsigned")) comparator_3 (.a(in_2), .b(4'b0101), .lt(\output [2]));  // open: gt, eq
  Comparator #(.width(4), .mode("unsigned")) comparator_4 (.a(in_2), .b(4'b1010), .gt(\output [3]));  // open: eq, lt

  assign \output [7:4] = 4'b0000;

  // Notes on the sheet:
  //   left
  //   right
  //   up
  //   down
endmodule

module some_cdm8e (
  input  [7:0] joystick,
  input  clk,
  output [7:0] cell_x,
  output [7:0] cell_y,
  output [7:0] adr
);

  wire addr_out, and_3_out, and_4_out, and_5_out, and_6_out, cdm_8_mark5_1_p1, cdm_8_mark5_1_p2,
       cdm_8_mark5_1_p4, cdm_8_mark5_1_p5, cdm_8_mark5_1_p6, cdm_8_mark5_1_p7, cdm_8_mark5_1_p8,
       cdm_8_mark5_1_p9, cell_x_out, cell_y_out, chngd_out, code, data, I_O_sel, in_out_prime, joystick_out,
       mem, nand_1_out, not_1_out, not_2_out, RAM, set_out;
  wire [0:0] undriven;
  wire [3:0] I_O_adr;
  wire [7:0] cdm_8_mark5_1_p13, cdm_8_mark5_1_p14, controlled_buffer_3_out, controlled_buffer_4_out,
       controlled_buffer_5_out, controlled_buffer_6_out, I_O_dat, register_1_q;
  wire [15:4] cdm_8_mark5_1_p12;

  // Probe on cdm_8_mark5_1_p1
  // Probe on cdm_8_mark5_1_p2
  and and_1 (I_O_sel, not_1_out, clk, data);
  Clock clock_1 ();  // open: out
  // Probe on cdm_8_mark5_1_p6
  // Probe on cdm_8_mark5_1_p5
  // Probe on cdm_8_mark5_1_p4
  not not_1 (not_1_out, nand_1_out);
  and and_2 (RAM, nand_1_out, data);
  // Probe on cdm_8_mark5_1_p7
  // Probe on cdm_8_mark5_1_p8
  // CdM_8_mark5 cdm_8_mark5_1: pin names not known; wires that end beside it: cdm_8_mark5_1_p1, cdm_8_mark5_1_p2, clk, cdm_8_mark5_1_p4, cdm_8_mark5_1_p5, cdm_8_mark5_1_p6, cdm_8_mark5_1_p7, cdm_8_mark5_1_p8, cdm_8_mark5_1_p9, mem, in_out_prime, {cdm_8_mark5_1_p12, I_O_adr}, cdm_8_mark5_1_p13, cdm_8_mark5_1_p14, in_out_prime
  nand nand_1 (nand_1_out, ~cdm_8_mark5_1_p12[4], cdm_8_mark5_1_p12[5], ~cdm_8_mark5_1_p12[6], ~cdm_8_mark5_1_p12[7]);  // NAND_Gate
  Decoder #(.disabled(0)) decoder_1 (.out0(code), .out1(data), .sel(cdm_8_mark5_1_p9), .en(mem));
  assign I_O_dat = not_2_out ? cdm_8_mark5_1_p13 : 8'bz;  // Controlled_Buffer controlled_buffer_1
  not not_2 (not_2_out, in_out_prime);
  assign cdm_8_mark5_1_p14 = in_out_prime ? I_O_dat : 8'bz;  // Controlled_Buffer controlled_buffer_2
  and chngd (chngd_out, I_O_sel, ~I_O_adr[0], ~I_O_adr[1], I_O_adr[2], ~I_O_adr[3]);  // AND_Gate
  and u_cell_x (cell_x_out, I_O_sel, I_O_adr[0], ~I_O_adr[1], I_O_adr[2], ~I_O_adr[3]);  // AND_Gate
  and u_cell_y (cell_y_out, I_O_sel, ~I_O_adr[0], I_O_adr[1], I_O_adr[2], ~I_O_adr[3]);  // AND_Gate
  and addr (addr_out, I_O_sel, I_O_adr[0], I_O_adr[1], I_O_adr[2], ~I_O_adr[3]);  // AND_Gate
  assign controlled_buffer_3_out = addr_out ? I_O_dat : 8'bz;  // Controlled_Buffer controlled_buffer_3
  assign controlled_buffer_4_out = chngd_out ? I_O_dat : 8'bz;  // Controlled_Buffer controlled_buffer_4
  ROM #(.addrWidth(16)) rom_1 (.addr({cdm_8_mark5_1_p12, I_O_adr}), .data(I_O_dat), .sel(code));
  RAM ram_1 (
    .addr({cdm_8_mark5_1_p12[7:4], I_O_adr}), .data(I_O_dat), .sel(RAM), .clk(clk), .ld(in_out_prime));  // open: clr
  and set (set_out, I_O_sel, ~I_O_adr[0], I_O_adr[1], ~I_O_adr[2], ~I_O_adr[3]);  // AND_Gate
  and and_3 (and_3_out, ~in_out_prime, cell_x_out);  // AND_Gate
  assign controlled_buffer_5_out = and_3_out ? I_O_dat : 8'bz;  // Controlled_Buffer controlled_buffer_5
  and and_4 (and_4_out, ~in_out_prime, cell_y_out);  // AND_Gate
  assign controlled_buffer_6_out = and_4_out ? I_O_dat : 8'bz;  // Controlled_Buffer controlled_buffer_6
  Register #(.trigger("high")) register_1 (
    .D(controlled_buffer_4_out), .en(chngd_out), .Q(register_1_q), .clk(chngd_out));  // open: clr
  and u_joystick (joystick_out, I_O_sel, I_O_adr[0], ~I_O_adr[1], ~I_O_adr[2], ~I_O_adr[3]);  // AND_Gate
  assign I_O_dat = set_out ? {{7{1'b0}}, undriven[0]} : 8'bz;  // Controlled_Buffer controlled_buffer_7
  Register #(.trigger("high")) register_2 (
    .D(controlled_buffer_5_out), .en(cell_x_out), .Q(cell_x), .clk(cell_x_out));  // open: clr
  Register #(.trigger("high")) register_3 (
    .D(controlled_buffer_6_out), .en(cell_y_out), .Q(cell_y), .clk(cell_y_out));  // open: clr
  // Probe on adr
  Register #(.trigger("high")) register_4 (
    .D(controlled_buffer_3_out), .en(addr_out), .Q(adr), .clk(addr_out));  // open: clr
  assign I_O_dat = joystick_out ? joystick : 8'bz;  // Controlled_Buffer controlled_buffer_8
  and and_5 (and_5_out, cell_x_out, in_out_prime);
  and and_6 (and_6_out, cell_y_out, in_out_prime);
  assign I_O_dat = and_5_out ? cell_x : 8'bz;  // Controlled_Buffer controlled_buffer_9
  assign I_O_dat = and_6_out ? cell_y : 8'bz;  // Controlled_Buffer controlled_buffer_10

  // Other names for the same wires on the sheet: rd_wr_prime = in_out_prime

  // Notes on the sheet:
  //   contents of rom_1 (hex, n*v repeats v):
  //   d0 7 d1 25 a4 d1 26 a4 0 e4 57 c0 c2 d2 21 ba 92 2f 92 2f d0 2 48 0 e0 8 d0 26 b1 8d a1 ee c d0 1 48
  //   0 e0 6 d0 26 b1 89 a1 d0 2 4c 0 e0 8 d0 25 b1 89 a1 ee c d0 1 4c 0 e0 6 d0 25 b1 8d a1 c6 d0 25 b0
  //   d1 26 b5 5*20 25 20 25 20 25 20 25 d0 27 a1 30 35 3a 3f c4 ee a8 d4
  //   высокий уровень!
endmodule

module displ_module (
  input  [7:0] lo,
  input  set_Lo,
  input  [7:0] hi,
  input  sel_Hi,
  input  [7:0] adr,
  input  sel_adr,
  input  clk,
  output [15:0] _1st_row,
  output [15:0] _2nd_row,
  output [15:0] _3rd_row,
  output [15:0] _4th_row,
  output [15:0] _5th_row,
  output [15:0] _6th_row,
  output [15:0] _7th_row,
  output [15:0] _8th_row,
  output [15:0] _9th_row,
  output [15:0] _10th_row,
  output [15:0] _11th_row,
  output [15:0] _12th_row,
  output [15:0] _13th_row,
  output [15:0] _14th_row,
  output [15:0] _15th_row,
  output [15:0] _16th_row
);

  wire demultiplexer_1_out0, demultiplexer_1_out1, demultiplexer_1_out2, demultiplexer_1_out3,
       demultiplexer_1_out4, demultiplexer_1_out5, demultiplexer_1_out6, demultiplexer_1_out7,
       demultiplexer_1_out8, demultiplexer_1_out9, demultiplexer_1_out10, demultiplexer_1_out11,
       demultiplexer_1_out12, demultiplexer_1_out13, demultiplexer_1_out14, demultiplexer_1_out15;
  wire [7:0] register_1_q, register_2_q, register_3_q;

  Register register_1 (.D(lo), .en(set_Lo), .Q(register_1_q), .clk(clk));  // open: clr
  Register register_2 (.D(hi), .en(sel_Hi), .Q(register_2_q), .clk(clk));  // open: clr
  Demultiplexer #(.select(4), .disabled(0)) demultiplexer_1 (
    .out0(demultiplexer_1_out0), .out1(demultiplexer_1_out1), .out2(demultiplexer_1_out2),
    .out3(demultiplexer_1_out3), .out4(demultiplexer_1_out4), .out5(demultiplexer_1_out5),
    .out6(demultiplexer_1_out6), .out7(demultiplexer_1_out7), .out8(demultiplexer_1_out8),
    .out9(demultiplexer_1_out9), .out10(demultiplexer_1_out10), .out11(demultiplexer_1_out11),
    .out12(demultiplexer_1_out12), .out13(demultiplexer_1_out13), .out14(demultiplexer_1_out14),
    .out15(demultiplexer_1_out15), .in(sel_adr), .sel(register_3_q[3:0]), .en(sel_adr));
  Register register_3 (.D(adr), .en(sel_adr), .Q(register_3_q), .clk(clk));  // open: clr
  // Probe on register_3_q
  Register #(.width(16)) register_4 (
    .D({register_2_q, register_1_q}), .en(demultiplexer_1_out0), .Q(_1st_row), .clk(clk));  // open: clr
  Register #(.width(16)) register_5 (
    .D({register_2_q, register_1_q}), .en(demultiplexer_1_out1), .Q(_2nd_row), .clk(clk));  // open: clr
  Register #(.width(16)) register_6 (
    .D({register_2_q, register_1_q}), .en(demultiplexer_1_out2), .Q(_3rd_row), .clk(clk));  // open: clr
  Register #(.width(16)) register_7 (
    .D({register_2_q, register_1_q}), .en(demultiplexer_1_out3), .Q(_4th_row), .clk(clk));  // open: clr
  Register #(.width(16)) register_8 (
    .D({register_2_q, register_1_q}), .en(demultiplexer_1_out4), .Q(_5th_row), .clk(clk));  // open: clr
  Register #(.width(16)) register_9 (
    .D({register_2_q, register_1_q}), .en(demultiplexer_1_out5), .Q(_6th_row), .clk(clk));  // open: clr
  Register #(.width(16)) register_10 (
    .D({register_2_q, register_1_q}), .en(demultiplexer_1_out6), .Q(_7th_row), .clk(clk));  // open: clr
  Register #(.width(16)) register_11 (
    .D({register_2_q, register_1_q}), .en(demultiplexer_1_out7), .Q(_8th_row), .clk(clk));  // open: clr
  Register #(.width(16)) register_12 (
    .D({register_2_q, register_1_q}), .en(demultiplexer_1_out8), .Q(_9th_row), .clk(clk));  // open: clr
  Register #(.width(16)) register_13 (
    .D({register_2_q, register_1_q}), .en(demultiplexer_1_out9), .Q(_10th_row), .clk(clk));  // open: clr
  Register #(.width(16)) register_14 (
    .D({register_2_q, register_1_q}), .en(demultiplexer_1_out10), .Q(_11th_row), .clk(clk));  // open: clr
  Register #(.width(16)) register_15 (
    .D({register_2_q, register_1_q}), .en(demultiplexer_1_out11), .Q(_12th_row), .clk(clk));  // open: clr
  Register #(.width(16)) register_16 (
    .D({register_2_q, register_1_q}), .en(demultiplexer_1_out12), .Q(_13th_row), .clk(clk));  // open: clr
  Register #(.width(16)) register_17 (
    .D({register_2_q, register_1_q}), .en(demultiplexer_1_out13), .Q(_14th_row), .clk(clk));  // open: clr
  Register #(.width(16)) register_18 (
    .D({register_2_q, register_1_q}), .en(demultiplexer_1_out14), .Q(_15th_row), .clk(clk));  // open: clr
  Register #(.width(16)) register_19 (
    .D({register_2_q, register_1_q}), .en(demultiplexer_1_out15), .Q(_16th_row), .clk(clk));  // open: clr
endmodule

module \cell  (
  input  ul_nb,
  input  up_nb,
  input  ur_nb,
  input  right_nb,
  input  left_nb,
  input  dr_nb,
  input  dl_nb,
  input  down_nb,
  input  set,
  input  clk,
  input  stop,
  output exit,
  output exit_2
);

  wire and_1_out, and_2_out, and_3_out, and_4_out, multiplexer_1_out, multiplexer_2_out, not_1_out,
       not_2_out, not_3_out, not_4_out, or_1_out, or_2_out, or_3_out;
  wire [2:0] adder_1_out, adder_2_out, adder_3_out, adder_4_out, adder_5_out, adder_6_out, adder_7_out,
       xnor_1_out, xnor_2_out;

  Adder #(.width(3)) adder_1 (.a({2'b00, ul_nb}), .b({2'b00, up_nb}), .out(adder_1_out));  // open: cin, cout
  Adder #(.width(3)) adder_2 (.a({2'b00, ur_nb}), .b({2'b00, right_nb}), .out(adder_2_out));  // open: cin, cout
  Adder #(.width(3)) adder_3 (.a({2'b00, left_nb}), .b({2'b00, dr_nb}), .out(adder_3_out));  // open: cin, cout
  Adder #(.width(3)) adder_4 (.a({2'b00, dl_nb}), .b({2'b00, down_nb}), .out(adder_4_out));  // open: cin, cout
  not not_1 (not_1_out, set);
  Adder #(.width(3)) adder_5 (.a(adder_1_out), .b(adder_2_out), .out(adder_5_out));  // open: cin, cout
  Adder #(.width(3)) adder_6 (.a(adder_3_out), .b(adder_4_out), .out(adder_6_out));  // open: cin, cout
  and and_1 (and_1_out, set, not_2_out);
  not not_2 (not_2_out, set);
  and and_2 (and_2_out, not_1_out, not_3_out);
  not not_3 (not_3_out, not_1_out);
  Adder #(.width(3)) adder_7 (.a(adder_5_out), .b(adder_6_out), .out(adder_7_out));  // open: cin, cout
  or or_1 (or_1_out, and_1_out, and_2_out);
  or or_2 (or_2_out, or_1_out, clk);
  D_Flip_Flop d_ff_1 (.clk(or_2_out), .D(multiplexer_2_out), .Q(exit));  // open: Qn, preset, en, reset
  assign xnor_1_out = ~(3'b010 ^ adder_7_out);  // XNOR_Gate xnor_1, 3 bits wide
  assign xnor_2_out = ~(adder_7_out ^ 3'b011);  // XNOR_Gate xnor_2, 3 bits wide
  and and_3 (and_3_out, xnor_2_out[0], xnor_2_out[1], xnor_2_out[2]);
  not not_4 (not_4_out, exit);
  Multiplexer #(.enable("false")) multiplexer_1 (.in0(exit), .in1(not_4_out), .out(multiplexer_1_out), .sel(set));
  and and_4 (and_4_out, exit, xnor_1_out[0], xnor_1_out[1], xnor_1_out[2]);
  or or_3 (or_3_out, and_4_out, and_3_out);
  Multiplexer #(.enable("false")) multiplexer_2 (
    .in0(or_3_out), .in1(multiplexer_1_out), .out(multiplexer_2_out), .sel(stop));

  assign exit_2 = exit;
endmodule

module row (
  input  nb1,
  input  nb2,
  input  nb3,
  input  nb4,
  input  nb5,
  input  nb6,
  input  nb7,
  input  nb8,
  input  nb9,
  input  nb10,
  input  nb11,
  input  nb12,
  input  nb13,
  input  nb14,
  input  nb15,
  input  nb16,
  input  nb17,
  input  nb18,
  input  nb19,
  input  nb20,
  input  nb21,
  input  nb22,
  input  nb23,
  input  nb24,
  input  nb25,
  input  nb26,
  input  nb27,
  input  nb28,
  input  nb29,
  input  nb30,
  input  nb31,
  input  nb32,
  input  clk,
  input  stop,
  input  set,
  input  [7:0] adr,
  output ex1,
  output ex2,
  output ex3,
  output ex4,
  output ex5,
  output ex6,
  output ex7,
  output ex8,
  output ex9,
  output ex10,
  output ex11,
  output ex12,
  output ex13,
  output ex14,
  output ex15,
  output ex16,
  output ex17,
  output ex18,
  output ex19,
  output ex20,
  output ex21,
  output ex22,
  output ex23,
  output ex24,
  output ex25,
  output ex26,
  output ex27,
  output ex28,
  output ex29,
  output ex30,
  output ex31,
  output ex32,
  output [15:0] \output ,
  output cell_out
);

  wire cell_1_exit_2, cell_2_exit_2, cell_3_exit_2, cell_4_exit_2, cell_5_exit_2, cell_6_exit_2,
       cell_7_exit_2, cell_8_exit_2, cell_9_exit_2, cell_10_exit_2, cell_11_exit_2, cell_12_exit_2,
       cell_13_exit_2, cell_14_exit_2, cell_15_exit_2, r_l, set1, set2, set3, set4, set5, set6, set7, set8,
       set9, set10, set11, set12, set13, set14, set15, set16;

  \cell  cell_1 (
    .ul_nb(nb16), .left_nb(r_l), .set(set1), .dl_nb(nb32), .ur_nb(nb2), .right_nb(ex2), .dr_nb(nb18),
    .up_nb(nb1), .down_nb(nb17), .exit(ex1), .exit_2(cell_1_exit_2), .clk(clk), .stop(stop));
  // Probe on adr
  \cell  cell_2 (
    .ul_nb(nb1), .left_nb(cell_1_exit_2), .set(set2), .dl_nb(nb17), .ur_nb(nb3), .right_nb(ex3),
    .dr_nb(nb19), .up_nb(nb2), .down_nb(nb18), .exit(ex2), .exit_2(cell_2_exit_2), .clk(clk), .stop(stop));
  Demultiplexer #(.select(4), .disabled(0)) demultiplexer_1 (
    .out0(set1), .out1(set2), .out2(set3), .out3(set4), .out4(set5), .out5(set6), .out6(set7), .out7(set8),
    .out8(set9), .out9(set10), .out10(set11), .out11(set12), .out12(set13), .out13(set14), .out14(set15),
    .out15(set16), .in(set), .sel(adr[3:0]), .en(set));
  \cell  cell_3 (
    .ul_nb(nb2), .left_nb(cell_2_exit_2), .set(set3), .dl_nb(nb18), .ur_nb(nb4), .right_nb(ex4),
    .dr_nb(nb20), .up_nb(nb3), .down_nb(nb19), .exit(ex3), .exit_2(cell_3_exit_2), .clk(clk), .stop(stop));
  \cell  cell_4 (
    .ul_nb(nb3), .left_nb(cell_3_exit_2), .set(set4), .dl_nb(nb19), .ur_nb(nb5), .right_nb(ex5),
    .dr_nb(nb21), .up_nb(nb4), .down_nb(nb20), .exit(ex4), .exit_2(cell_4_exit_2), .clk(clk), .stop(stop));
  \cell  cell_5 (
    .ul_nb(nb4), .left_nb(cell_4_exit_2), .set(set5), .dl_nb(nb20), .ur_nb(nb6), .right_nb(ex6),
    .dr_nb(nb22), .up_nb(nb5), .down_nb(nb21), .exit(ex5), .exit_2(cell_5_exit_2), .clk(clk), .stop(stop));
  \cell  cell_6 (
    .ul_nb(nb5), .left_nb(cell_5_exit_2), .set(set6), .dl_nb(nb21), .ur_nb(nb7), .right_nb(ex7),
    .dr_nb(nb23), .up_nb(nb6), .down_nb(nb22), .exit(ex6), .exit_2(cell_6_exit_2), .clk(clk), .stop(stop));
  \cell  cell_7 (
    .ul_nb(nb6), .left_nb(cell_6_exit_2), .set(set7), .dl_nb(nb22), .ur_nb(nb8), .right_nb(ex8),
    .dr_nb(nb24), .up_nb(nb7), .down_nb(nb23), .exit(ex7), .exit_2(cell_7_exit_2), .clk(clk), .stop(stop));
  \cell  cell_8 (
    .ul_nb(nb7), .left_nb(cell_7_exit_2), .set(set8), .dl_nb(nb23), .ur_nb(nb9), .right_nb(ex9),
    .dr_nb(nb25), .up_nb(nb8), .down_nb(nb24), .exit(ex8), .exit_2(cell_8_exit_2), .clk(clk), .stop(stop));
  Multiplexer #(.select(4), .enable("false")) multiplexer_1 (
    .in0(ex1), .in1(ex2), .in2(ex3), .in3(ex4), .in4(ex5), .in5(ex6), .in6(ex7), .in7(ex8), .in8(ex9),
    .in9(ex10), .in10(ex11), .in11(ex12), .in12(ex13), .in13(ex14), .in14(ex15), .in15(ex16), .out(cell_out),
    .sel(adr[3:0]));
  \cell  cell_9 (
    .ul_nb(nb8), .left_nb(cell_8_exit_2), .set(set9), .dl_nb(nb24), .ur_nb(nb10), .right_nb(ex10),
    .dr_nb(nb26), .up_nb(nb9), .down_nb(nb25), .exit(ex9), .exit_2(cell_9_exit_2), .clk(clk), .stop(stop));
  \cell  cell_10 (
    .ul_nb(nb9), .left_nb(cell_9_exit_2), .set(set10), .dl_nb(nb25), .ur_nb(nb11), .right_nb(ex11),
    .dr_nb(nb27), .up_nb(nb10), .down_nb(nb26), .exit(ex10), .exit_2(cell_10_exit_2), .clk(clk), .stop(stop));
  \cell  cell_11 (
    .ul_nb(nb10), .left_nb(cell_10_exit_2), .set(set11), .dl_nb(nb26), .ur_nb(nb12), .right_nb(ex12),
    .dr_nb(nb28), .up_nb(nb11), .down_nb(nb27), .exit(ex11), .exit_2(cell_11_exit_2), .clk(clk), .stop(stop));
  \cell  cell_12 (
    .ul_nb(nb11), .left_nb(cell_11_exit_2), .set(set12), .dl_nb(nb27), .ur_nb(nb13), .right_nb(ex13),
    .dr_nb(nb29), .up_nb(nb12), .down_nb(nb28), .exit(ex12), .exit_2(cell_12_exit_2), .clk(clk), .stop(stop));
  \cell  cell_13 (
    .ul_nb(nb12), .left_nb(cell_12_exit_2), .set(set13), .dl_nb(nb28), .ur_nb(nb14), .right_nb(ex14),
    .dr_nb(nb30), .up_nb(nb13), .down_nb(nb29), .exit(ex13), .exit_2(cell_13_exit_2), .clk(clk), .stop(stop));
  \cell  cell_14 (
    .ul_nb(nb13), .left_nb(cell_13_exit_2), .set(set14), .dl_nb(nb29), .ur_nb(nb15), .right_nb(ex15),
    .dr_nb(nb31), .up_nb(nb14), .down_nb(nb30), .exit(ex14), .exit_2(cell_14_exit_2), .clk(clk), .stop(stop));
  \cell  cell_15 (
    .ul_nb(nb14), .left_nb(cell_14_exit_2), .set(set15), .dl_nb(nb30), .ur_nb(nb16), .right_nb(ex16),
    .dr_nb(nb32), .up_nb(nb15), .down_nb(nb31), .exit(ex15), .exit_2(cell_15_exit_2), .clk(clk), .stop(stop));
  \cell  cell_16 (
    .ul_nb(nb15), .left_nb(cell_15_exit_2), .set(set16), .dl_nb(nb31), .ur_nb(nb1), .right_nb(ex1),
    .dr_nb(nb17), .up_nb(nb16), .down_nb(nb32), .exit(ex16), .exit_2(r_l), .clk(clk), .stop(stop));

  assign ex17 = ex1;
  assign ex18 = ex2;
  assign ex19 = ex3;
  assign ex20 = ex4;
  assign ex21 = ex5;
  assign ex22 = ex6;
  assign ex23 = ex7;
  assign ex24 = ex8;
  assign ex25 = ex9;
  assign ex26 = ex10;
  assign ex27 = ex11;
  assign ex28 = ex12;
  assign ex29 = ex13;
  assign ex30 = ex14;
  assign ex31 = ex15;
  assign ex32 = ex16;
  assign \output  = {ex1, ex2, ex3, ex4, ex5, ex6, ex7, ex8, ex9, ex10, ex11, ex12, ex13, ex14, ex15, ex16};

  // Other names for the same wires on the sheet: adr_t[3:0] = adr[3:0]; ld_to_rd_nb = nb17; lu_to_ru_nb = nb1;
  //   out15 = ex16; out14 = ex15; out13 = ex14; out12 = ex13; out11 = ex12; out10 = ex11; out9 = ex10; out8 = ex9;
  //   out7 = ex8; out6 = ex7; out5 = ex6; out4 = ex5; out3 = ex4; out2 = ex3; out1 = ex2; l_r = ex1; out0 = ex1;
  //   rd_to_ld_nb = nb32; ru_to_lu_nb = nb16
endmodule

module game (
  input  clk,
  input  [7:0] adr,
  input  stop,
  input  set,
  output [15:0] halted,
  output [15:0] halted_2,
  output [15:0] halted_3,
  output cell_out,
  output [15:0] halted_4,
  output [15:0] halted_5,
  output [15:0] halted_6,
  output [15:0] halted_7,
  output [15:0] halted_8,
  output [15:0] halted_9,
  output [15:0] halted_10,
  output [15:0] halted_11,
  output [15:0] halted_12,
  output [15:0] halted_13,
  output [15:0] halted_14,
  output [15:0] halted_15,
  output [15:0] halted_16
);

  wire clk_t, out1, out2, out3, out4, out5, out6, out7, out8, out9, out10, out11, out12, out13, out14, out15,
       out16, row_1_ex17, row_1_ex18, row_1_ex19, row_1_ex20, row_1_ex21, row_1_ex22, row_1_ex23, row_1_ex24,
       row_1_ex25, row_1_ex26, row_1_ex27, row_1_ex28, row_1_ex29, row_1_ex30, row_1_ex31, row_1_ex32,
       row_2_ex1, row_2_ex2, row_2_ex3, row_2_ex4, row_2_ex5, row_2_ex6, row_2_ex7, row_2_ex8, row_2_ex9,
       row_2_ex10, row_2_ex11, row_2_ex12, row_2_ex13, row_2_ex14, row_2_ex15, row_2_ex16, row_2_ex17,
       row_2_ex18, row_2_ex19, row_2_ex20, row_2_ex21, row_2_ex22, row_2_ex23, row_2_ex24, row_2_ex25,
       row_2_ex26, row_2_ex27, row_2_ex28, row_2_ex29, row_2_ex30, row_2_ex31, row_2_ex32, row_3_ex1,
       row_3_ex2, row_3_ex3, row_3_ex4, row_3_ex5, row_3_ex6, row_3_ex7, row_3_ex8, row_3_ex9, row_3_ex10,
       row_3_ex11, row_3_ex12, row_3_ex13, row_3_ex14, row_3_ex15, row_3_ex16, row_3_ex17, row_3_ex18,
       row_3_ex19, row_3_ex20, row_3_ex21, row_3_ex22, row_3_ex23, row_3_ex24, row_3_ex25, row_3_ex26,
       row_3_ex27, row_3_ex28, row_3_ex29, row_3_ex30, row_3_ex31, row_3_ex32, row_4_ex1, row_4_ex2,
       row_4_ex3, row_4_ex4, row_4_ex5, row_4_ex6, row_4_ex7, row_4_ex8, row_4_ex9, row_4_ex10, row_4_ex11,
       row_4_ex12, row_4_ex13, row_4_ex14, row_4_ex15, row_4_ex16, row_4_ex17, row_4_ex18, row_4_ex19,
       row_4_ex20, row_4_ex21, row_4_ex22, row_4_ex23, row_4_ex24, row_4_ex25, row_4_ex26, row_4_ex27,
       row_4_ex28, row_4_ex29, row_4_ex30, row_4_ex31, row_4_ex32, row_5_ex1, row_5_ex2, row_5_ex3,
       row_5_ex4, row_5_ex5, row_5_ex6, row_5_ex7, row_5_ex8, row_5_ex9, row_5_ex10, row_5_ex11, row_5_ex12,
       row_5_ex13, row_5_ex14, row_5_ex15, row_5_ex16, row_5_ex17, row_5_ex18, row_5_ex19, row_5_ex20,
       row_5_ex21, row_5_ex22, row_5_ex23, row_5_ex24, row_5_ex25, row_5_ex26, row_5_ex27, row_5_ex28,
       row_5_ex29, row_5_ex30, row_5_ex31, row_5_ex32, row_6_ex1, row_6_ex2, row_6_ex3, row_6_ex4, row_6_ex5,
       row_6_ex6, row_6_ex7, row_6_ex8, row_6_ex9, row_6_ex10, row_6_ex11, row_6_ex12, row_6_ex13,
       row_6_ex14, row_6_ex15, row_6_ex16, row_6_ex17, row_6_ex18, row_6_ex19, row_6_ex20, row_6_ex21,
       row_6_ex22, row_6_ex23, row_6_ex24, row_6_ex25, row_6_ex26, row_6_ex27, row_6_ex28, row_6_ex29,
       row_6_ex30, row_6_ex31, row_6_ex32, row_7_ex1, row_7_ex2, row_7_ex3, row_7_ex4, row_7_ex5, row_7_ex6,
       row_7_ex7, row_7_ex8, row_7_ex9, row_7_ex10, row_7_ex11, row_7_ex12, row_7_ex13, row_7_ex14,
       row_7_ex15, row_7_ex16, row_7_ex17, row_7_ex18, row_7_ex19, row_7_ex20, row_7_ex21, row_7_ex22,
       row_7_ex23, row_7_ex24, row_7_ex25, row_7_ex26, row_7_ex27, row_7_ex28, row_7_ex29, row_7_ex30,
       row_7_ex31, row_7_ex32, row_8_ex1, row_8_ex2, row_8_ex3, row_8_ex4, row_8_ex5, row_8_ex6, row_8_ex7,
       row_8_ex8, row_8_ex9, row_8_ex10, row_8_ex11, row_8_ex12, row_8_ex13, row_8_ex14, row_8_ex15,
       row_8_ex16, row_8_ex17, row_8_ex18, row_8_ex19, row_8_ex20, row_8_ex21, row_8_ex22, row_8_ex23,
       row_8_ex24, row_8_ex25, row_8_ex26, row_8_ex27, row_8_ex28, row_8_ex29, row_8_ex30, row_8_ex31,
       row_8_ex32, row_9_ex1, row_9_ex2, row_9_ex3, row_9_ex4, row_9_ex5, row_9_ex6, row_9_ex7, row_9_ex8,
       row_9_ex9, row_9_ex10, row_9_ex11, row_9_ex12, row_9_ex13, row_9_ex14, row_9_ex15, row_9_ex16,
       row_9_ex17, row_9_ex18, row_9_ex19, row_9_ex20, row_9_ex21, row_9_ex22, row_9_ex23, row_9_ex24,
       row_9_ex25, row_9_ex26, row_9_ex27, row_9_ex28, row_9_ex29, row_9_ex30, row_9_ex31, row_9_ex32,
       row_10_ex1, row_10_ex2, row_10_ex3, row_10_ex4, row_10_ex5, row_10_ex6, row_10_ex7, row_10_ex8,
       row_10_ex9, row_10_ex10, row_10_ex11, row_10_ex12, row_10_ex13, row_10_ex14, row_10_ex15, row_10_ex16,
       row_10_ex17, row_10_ex18, row_10_ex19, row_10_ex20, row_10_ex21, row_10_ex22, row_10_ex23,
       row_10_ex24, row_10_ex25, row_10_ex26, row_10_ex27, row_10_ex28, row_10_ex29, row_10_ex30,
       row_10_ex31, row_10_ex32, row_11_ex1, row_11_ex2, row_11_ex3, row_11_ex4, row_11_ex5, row_11_ex6,
       row_11_ex7, row_11_ex8, row_11_ex9, row_11_ex10, row_11_ex11, row_11_ex12, row_11_ex13, row_11_ex14,
       row_11_ex15, row_11_ex16, row_11_ex17, row_11_ex18, row_11_ex19, row_11_ex20, row_11_ex21,
       row_11_ex22, row_11_ex23, row_11_ex24, row_11_ex25, row_11_ex26, row_11_ex27, row_11_ex28,
       row_11_ex29, row_11_ex30, row_11_ex31, row_11_ex32, row_12_ex1, row_12_ex2, row_12_ex3, row_12_ex4,
       row_12_ex5, row_12_ex6, row_12_ex7, row_12_ex8, row_12_ex9, row_12_ex10, row_12_ex11, row_12_ex12,
       row_12_ex13, row_12_ex14, row_12_ex15, row_12_ex16, row_12_ex17, row_12_ex18, row_12_ex19,
       row_12_ex20, row_12_ex21, row_12_ex22, row_12_ex23, row_12_ex24, row_12_ex25, row_12_ex26,
       row_12_ex27, row_12_ex28, row_12_ex29, row_12_ex30, row_12_ex31, row_12_ex32, row_13_ex1, row_13_ex2,
       row_13_ex3, row_13_ex4, row_13_ex5, row_13_ex6, row_13_ex7, row_13_ex8, row_13_ex9, row_13_ex10,
       row_13_ex11, row_13_ex12, row_13_ex13, row_13_ex14, row_13_ex15, row_13_ex16, row_13_ex17,
       row_13_ex18, row_13_ex19, row_13_ex20, row_13_ex21, row_13_ex22, row_13_ex23, row_13_ex24,
       row_13_ex25, row_13_ex26, row_13_ex27, row_13_ex28, row_13_ex29, row_13_ex30, row_13_ex31,
       row_13_ex32, row_14_ex1, row_14_ex2, row_14_ex3, row_14_ex4, row_14_ex5, row_14_ex6, row_14_ex7,
       row_14_ex8, row_14_ex9, row_14_ex10, row_14_ex11, row_14_ex12, row_14_ex13, row_14_ex14, row_14_ex15,
       row_14_ex16, row_14_ex17, row_14_ex18, row_14_ex19, row_14_ex20, row_14_ex21, row_14_ex22,
       row_14_ex23, row_14_ex24, row_14_ex25, row_14_ex26, row_14_ex27, row_14_ex28, row_14_ex29,
       row_14_ex30, row_14_ex31, row_14_ex32, row_15_ex1, row_15_ex2, row_15_ex3, row_15_ex4, row_15_ex5,
       row_15_ex6, row_15_ex7, row_15_ex8, row_15_ex9, row_15_ex10, row_15_ex11, row_15_ex12, row_15_ex13,
       row_15_ex14, row_15_ex15, row_15_ex16, row_15_ex17, row_15_ex18, row_15_ex19, row_15_ex20,
       row_15_ex21, row_15_ex22, row_15_ex23, row_15_ex24, row_15_ex25, row_15_ex26, row_15_ex27,
       row_15_ex28, row_15_ex29, row_15_ex30, row_15_ex31, row_15_ex32, row_16_ex1, row_16_ex2, row_16_ex3,
       row_16_ex4, row_16_ex5, row_16_ex6, row_16_ex7, row_16_ex8, row_16_ex9, row_16_ex10, row_16_ex11,
       row_16_ex12, row_16_ex13, row_16_ex14, row_16_ex15, row_16_ex16, set1, set2, set3, set4, set5, set6,
       set7, set8, set9, set10, set11, set12, set13, set14, set15, set16, tun0, tun1, tun2, tun3, tun4, tun5,
       tun6, tun7, tun8, tun9, tun10, tun11, tun12, tun13, tun14, tun15, tun16, tun17, tun18, tun19, tun20,
       tun21, tun22, tun23, tun24, tun25, tun26, tun27, tun28, tun29, tun30, tun31;

  Clock clock_1 ();  // open: out
  and and_1 (clk_t, clk, ~stop);  // AND_Gate
  row row_1 (
    .clk(clk_t), .ex1(tun1), .nb1(tun0), .ex2(tun3), .nb2(tun2), .ex3(tun5), .nb3(tun4), .ex4(tun7),
    .nb4(tun6), .ex5(tun9), .nb5(tun8), .ex6(tun11), .nb6(tun10), .ex7(tun13), .nb7(tun12), .ex8(tun15),
    .nb8(tun14), .ex9(tun17), .nb9(tun16), .ex10(tun19), .nb10(tun18), .ex11(tun21), .nb11(tun20),
    .ex12(tun23), .nb12(tun22), .ex13(tun25), .nb13(tun24), .ex14(tun27), .nb14(tun26), .ex15(tun29),
    .nb15(tun28), .ex16(tun31), .nb16(tun30), .ex17(row_1_ex17), .nb17(row_2_ex1), .ex18(row_1_ex18),
    .nb18(row_2_ex2), .ex19(row_1_ex19), .nb19(row_2_ex3), .ex20(row_1_ex20), .nb20(row_2_ex4),
    .ex21(row_1_ex21), .nb21(row_2_ex5), .ex22(row_1_ex22), .nb22(row_2_ex6), .ex23(row_1_ex23),
    .nb23(row_2_ex7), .ex24(row_1_ex24), .nb24(row_2_ex8), .ex25(row_1_ex25), .nb25(row_2_ex9),
    .ex26(row_1_ex26), .nb26(row_2_ex10), .ex27(row_1_ex27), .nb27(row_2_ex11), .ex28(row_1_ex28),
    .nb28(row_2_ex12), .ex29(row_1_ex29), .nb29(row_2_ex13), .ex30(row_1_ex30), .nb30(row_2_ex14),
    .ex31(row_1_ex31), .nb31(row_2_ex15), .ex32(row_1_ex32), .nb32(row_2_ex16), .set(set1),
    .\output (halted), .cell_out(out1), .stop(stop), .adr(adr));
  row row_2 (
    .clk(clk_t), .ex1(row_2_ex1), .nb1(row_1_ex17), .ex2(row_2_ex2), .nb2(row_1_ex18), .ex3(row_2_ex3),
    .nb3(row_1_ex19), .ex4(row_2_ex4), .nb4(row_1_ex20), .ex5(row_2_ex5), .nb5(row_1_ex21), .ex6(row_2_ex6),
    .nb6(row_1_ex22), .ex7(row_2_ex7), .nb7(row_1_ex23), .ex8(row_2_ex8), .nb8(row_1_ex24), .ex9(row_2_ex9),
    .nb9(row_1_ex25), .ex10(row_2_ex10), .nb10(row_1_ex26), .ex11(row_2_ex11), .nb11(row_1_ex27),
    .ex12(row_2_ex12), .nb12(row_1_ex28), .ex13(row_2_ex13), .nb13(row_1_ex29), .ex14(row_2_ex14),
    .nb14(row_1_ex30), .ex15(row_2_ex15), .nb15(row_1_ex31), .ex16(row_2_ex16), .nb16(row_1_ex32),
    .ex17(row_2_ex17), .nb17(row_3_ex1), .ex18(row_2_ex18), .nb18(row_3_ex2), .ex19(row_2_ex19),
    .nb19(row_3_ex3), .ex20(row_2_ex20), .nb20(row_3_ex4), .ex21(row_2_ex21), .nb21(row_3_ex5),
    .ex22(row_2_ex22), .nb22(row_3_ex6), .ex23(row_2_ex23), .nb23(row_3_ex7), .ex24(row_2_ex24),
    .nb24(row_3_ex8), .ex25(row_2_ex25), .nb25(row_3_ex9), .ex26(row_2_ex26), .nb26(row_3_ex10),
    .ex27(row_2_ex27), .nb27(row_3_ex11), .ex28(row_2_ex28), .nb28(row_3_ex12), .ex29(row_2_ex29),
    .nb29(row_3_ex13), .ex30(row_2_ex30), .nb30(row_3_ex14), .ex31(row_2_ex31), .nb31(row_3_ex15),
    .ex32(row_2_ex32), .nb32(row_3_ex16), .set(set2), .\output (halted_2), .cell_out(out2), .stop(stop),
    .adr(adr));
  row row_3 (
    .clk(clk_t), .ex1(row_3_ex1), .nb1(row_2_ex17), .ex2(row_3_ex2), .nb2(row_2_ex18), .ex3(row_3_ex3),
    .nb3(row_2_ex19), .ex4(row_3_ex4), .nb4(row_2_ex20), .ex5(row_3_ex5), .nb5(row_2_ex21), .ex6(row_3_ex6),
    .nb6(row_2_ex22), .ex7(row_3_ex7), .nb7(row_2_ex23), .ex8(row_3_ex8), .nb8(row_2_ex24), .ex9(row_3_ex9),
    .nb9(row_2_ex25), .ex10(row_3_ex10), .nb10(row_2_ex26), .ex11(row_3_ex11), .nb11(row_2_ex27),
    .ex12(row_3_ex12), .nb12(row_2_ex28), .ex13(row_3_ex13), .nb13(row_2_ex29), .ex14(row_3_ex14),
    .nb14(row_2_ex30), .ex15(row_3_ex15), .nb15(row_2_ex31), .ex16(row_3_ex16), .nb16(row_2_ex32),
    .ex17(row_3_ex17), .nb17(row_4_ex1), .ex18(row_3_ex18), .nb18(row_4_ex2), .ex19(row_3_ex19),
    .nb19(row_4_ex3), .ex20(row_3_ex20), .nb20(row_4_ex4), .ex21(row_3_ex21), .nb21(row_4_ex5),
    .ex22(row_3_ex22), .nb22(row_4_ex6), .ex23(row_3_ex23), .nb23(row_4_ex7), .ex24(row_3_ex24),
    .nb24(row_4_ex8), .ex25(row_3_ex25), .nb25(row_4_ex9), .ex26(row_3_ex26), .nb26(row_4_ex10),
    .ex27(row_3_ex27), .nb27(row_4_ex11), .ex28(row_3_ex28), .nb28(row_4_ex12), .ex29(row_3_ex29),
    .nb29(row_4_ex13), .ex30(row_3_ex30), .nb30(row_4_ex14), .ex31(row_3_ex31), .nb31(row_4_ex15),
    .ex32(row_3_ex32), .nb32(row_4_ex16), .set(set3), .\output (halted_3), .cell_out(out3), .stop(stop),
    .adr(adr));
  row row_4 (
    .clk(clk_t), .ex1(row_4_ex1), .nb1(row_3_ex17), .ex2(row_4_ex2), .nb2(row_3_ex18), .ex3(row_4_ex3),
    .nb3(row_3_ex19), .ex4(row_4_ex4), .nb4(row_3_ex20), .ex5(row_4_ex5), .nb5(row_3_ex21), .ex6(row_4_ex6),
    .nb6(row_3_ex22), .ex7(row_4_ex7), .nb7(row_3_ex23), .ex8(row_4_ex8), .nb8(row_3_ex24), .ex9(row_4_ex9),
    .nb9(row_3_ex25), .ex10(row_4_ex10), .nb10(row_3_ex26), .ex11(row_4_ex11), .nb11(row_3_ex27),
    .ex12(row_4_ex12), .nb12(row_3_ex28), .ex13(row_4_ex13), .nb13(row_3_ex29), .ex14(row_4_ex14),
    .nb14(row_3_ex30), .ex15(row_4_ex15), .nb15(row_3_ex31), .ex16(row_4_ex16), .nb16(row_3_ex32),
    .ex17(row_4_ex17), .nb17(row_5_ex1), .ex18(row_4_ex18), .nb18(row_5_ex2), .ex19(row_4_ex19),
    .nb19(row_5_ex3), .ex20(row_4_ex20), .nb20(row_5_ex4), .ex21(row_4_ex21), .nb21(row_5_ex5),
    .ex22(row_4_ex22), .nb22(row_5_ex6), .ex23(row_4_ex23), .nb23(row_5_ex7), .ex24(row_4_ex24),
    .nb24(row_5_ex8), .ex25(row_4_ex25), .nb25(row_5_ex9), .ex26(row_4_ex26), .nb26(row_5_ex10),
    .ex27(row_4_ex27), .nb27(row_5_ex11), .ex28(row_4_ex28), .nb28(row_5_ex12), .ex29(row_4_ex29),
    .nb29(row_5_ex13), .ex30(row_4_ex30), .nb30(row_5_ex14), .ex31(row_4_ex31), .nb31(row_5_ex15),
    .ex32(row_4_ex32), .nb32(row_5_ex16), .set(set4), .\output (halted_4), .cell_out(out4), .stop(stop),
    .adr(adr));
  row row_5 (
    .clk(clk_t), .ex1(row_5_ex1), .nb1(row_4_ex17), .ex2(row_5_ex2), .nb2(row_4_ex18), .ex3(row_5_ex3),
    .nb3(row_4_ex19), .ex4(row_5_ex4), .nb4(row_4_ex20), .ex5(row_5_ex5), .nb5(row_4_ex21), .ex6(row_5_ex6),
    .nb6(row_4_ex22), .ex7(row_5_ex7), .nb7(row_4_ex23), .ex8(row_5_ex8), .nb8(row_4_ex24), .ex9(row_5_ex9),
    .nb9(row_4_ex25), .ex10(row_5_ex10), .nb10(row_4_ex26), .ex11(row_5_ex11), .nb11(row_4_ex27),
    .ex12(row_5_ex12), .nb12(row_4_ex28), .ex13(row_5_ex13), .nb13(row_4_ex29), .ex14(row_5_ex14),
    .nb14(row_4_ex30), .ex15(row_5_ex15), .nb15(row_4_ex31), .ex16(row_5_ex16), .nb16(row_4_ex32),
    .ex17(row_5_ex17), .nb17(row_6_ex1), .ex18(row_5_ex18), .nb18(row_6_ex2), .ex19(row_5_ex19),
    .nb19(row_6_ex3), .ex20(row_5_ex20), .nb20(row_6_ex4), .ex21(row_5_ex21), .nb21(row_6_ex5),
    .ex22(row_5_ex22), .nb22(row_6_ex6), .ex23(row_5_ex23), .nb23(row_6_ex7), .ex24(row_5_ex24),
    .nb24(row_6_ex8), .ex25(row_5_ex25), .nb25(row_6_ex9), .ex26(row_5_ex26), .nb26(row_6_ex10),
    .ex27(row_5_ex27), .nb27(row_6_ex11), .ex28(row_5_ex28), .nb28(row_6_ex12), .ex29(row_5_ex29),
    .nb29(row_6_ex13), .ex30(row_5_ex30), .nb30(row_6_ex14), .ex31(row_5_ex31), .nb31(row_6_ex15),
    .ex32(row_5_ex32), .nb32(row_6_ex16), .set(set5), .\output (halted_5), .cell_out(out5), .stop(stop),
    .adr(adr));
  row row_6 (
    .clk(clk_t), .ex1(row_6_ex1), .nb1(row_5_ex17), .ex2(row_6_ex2), .nb2(row_5_ex18), .ex3(row_6_ex3),
    .nb3(row_5_ex19), .ex4(row_6_ex4), .nb4(row_5_ex20), .ex5(row_6_ex5), .nb5(row_5_ex21), .ex6(row_6_ex6),
    .nb6(row_5_ex22), .ex7(row_6_ex7), .nb7(row_5_ex23), .ex8(row_6_ex8), .nb8(row_5_ex24), .ex9(row_6_ex9),
    .nb9(row_5_ex25), .ex10(row_6_ex10), .nb10(row_5_ex26), .ex11(row_6_ex11), .nb11(row_5_ex27),
    .ex12(row_6_ex12), .nb12(row_5_ex28), .ex13(row_6_ex13), .nb13(row_5_ex29), .ex14(row_6_ex14),
    .nb14(row_5_ex30), .ex15(row_6_ex15), .nb15(row_5_ex31), .ex16(row_6_ex16), .nb16(row_5_ex32),
    .ex17(row_6_ex17), .nb17(row_7_ex1), .ex18(row_6_ex18), .nb18(row_7_ex2), .ex19(row_6_ex19),
    .nb19(row_7_ex3), .ex20(row_6_ex20), .nb20(row_7_ex4), .ex21(row_6_ex21), .nb21(row_7_ex5),
    .ex22(row_6_ex22), .nb22(row_7_ex6), .ex23(row_6_ex23), .nb23(row_7_ex7), .ex24(row_6_ex24),
    .nb24(row_7_ex8), .ex25(row_6_ex25), .nb25(row_7_ex9), .ex26(row_6_ex26), .nb26(row_7_ex10),
    .ex27(row_6_ex27), .nb27(row_7_ex11), .ex28(row_6_ex28), .nb28(row_7_ex12), .ex29(row_6_ex29),
    .nb29(row_7_ex13), .ex30(row_6_ex30), .nb30(row_7_ex14), .ex31(row_6_ex31), .nb31(row_7_ex15),
    .ex32(row_6_ex32), .nb32(row_7_ex16), .set(set6), .\output (halted_6), .cell_out(out6), .stop(stop),
    .adr(adr));
  row row_7 (
    .clk(clk_t), .ex1(row_7_ex1), .nb1(row_6_ex17), .ex2(row_7_ex2), .nb2(row_6_ex18), .ex3(row_7_ex3),
    .nb3(row_6_ex19), .ex4(row_7_ex4), .nb4(row_6_ex20), .ex5(row_7_ex5), .nb5(row_6_ex21), .ex6(row_7_ex6),
    .nb6(row_6_ex22), .ex7(row_7_ex7), .nb7(row_6_ex23), .ex8(row_7_ex8), .nb8(row_6_ex24), .ex9(row_7_ex9),
    .nb9(row_6_ex25), .ex10(row_7_ex10), .nb10(row_6_ex26), .ex11(row_7_ex11), .nb11(row_6_ex27),
    .ex12(row_7_ex12), .nb12(row_6_ex28), .ex13(row_7_ex13), .nb13(row_6_ex29), .ex14(row_7_ex14),
    .nb14(row_6_ex30), .ex15(row_7_ex15), .nb15(row_6_ex31), .ex16(row_7_ex16), .nb16(row_6_ex32),
    .ex17(row_7_ex17), .nb17(row_8_ex1), .ex18(row_7_ex18), .nb18(row_8_ex2), .ex19(row_7_ex19),
    .nb19(row_8_ex3), .ex20(row_7_ex20), .nb20(row_8_ex4), .ex21(row_7_ex21), .nb21(row_8_ex5),
    .ex22(row_7_ex22), .nb22(row_8_ex6), .ex23(row_7_ex23), .nb23(row_8_ex7), .ex24(row_7_ex24),
    .nb24(row_8_ex8), .ex25(row_7_ex25), .nb25(row_8_ex9), .ex26(row_7_ex26), .nb26(row_8_ex10),
    .ex27(row_7_ex27), .nb27(row_8_ex11), .ex28(row_7_ex28), .nb28(row_8_ex12), .ex29(row_7_ex29),
    .nb29(row_8_ex13), .ex30(row_7_ex30), .nb30(row_8_ex14), .ex31(row_7_ex31), .nb31(row_8_ex15),
    .ex32(row_7_ex32), .nb32(row_8_ex16), .set(set7), .\output (halted_7), .cell_out(out7), .stop(stop),
    .adr(adr));
  row row_8 (
    .clk(clk_t), .ex1(row_8_ex1), .nb1(row_7_ex17), .ex2(row_8_ex2), .nb2(row_7_ex18), .ex3(row_8_ex3),
    .nb3(row_7_ex19), .ex4(row_8_ex4), .nb4(row_7_ex20), .ex5(row_8_ex5), .nb5(row_7_ex21), .ex6(row_8_ex6),
    .nb6(row_7_ex22), .ex7(row_8_ex7), .nb7(row_7_ex23), .ex8(row_8_ex8), .nb8(row_7_ex24), .ex9(row_8_ex9),
    .nb9(row_7_ex25), .ex10(row_8_ex10), .nb10(row_7_ex26), .ex11(row_8_ex11), .nb11(row_7_ex27),
    .ex12(row_8_ex12), .nb12(row_7_ex28), .ex13(row_8_ex13), .nb13(row_7_ex29), .ex14(row_8_ex14),
    .nb14(row_7_ex30), .ex15(row_8_ex15), .nb15(row_7_ex31), .ex16(row_8_ex16), .nb16(row_7_ex32),
    .ex17(row_8_ex17), .nb17(row_9_ex1), .ex18(row_8_ex18), .nb18(row_9_ex2), .ex19(row_8_ex19),
    .nb19(row_9_ex3), .ex20(row_8_ex20), .nb20(row_9_ex4), .ex21(row_8_ex21), .nb21(row_9_ex5),
    .ex22(row_8_ex22), .nb22(row_9_ex6), .ex23(row_8_ex23), .nb23(row_9_ex7), .ex24(row_8_ex24),
    .nb24(row_9_ex8), .ex25(row_8_ex25), .nb25(row_9_ex9), .ex26(row_8_ex26), .nb26(row_9_ex10),
    .ex27(row_8_ex27), .nb27(row_9_ex11), .ex28(row_8_ex28), .nb28(row_9_ex12), .ex29(row_8_ex29),
    .nb29(row_9_ex13), .ex30(row_8_ex30), .nb30(row_9_ex14), .ex31(row_8_ex31), .nb31(row_9_ex15),
    .ex32(row_8_ex32), .nb32(row_9_ex16), .set(set8), .\output (halted_8), .cell_out(out8), .stop(stop),
    .adr(adr));
  row row_9 (
    .clk(clk_t), .ex1(row_9_ex1), .nb1(row_8_ex17), .ex2(row_9_ex2), .nb2(row_8_ex18), .ex3(row_9_ex3),
    .nb3(row_8_ex19), .ex4(row_9_ex4), .nb4(row_8_ex20), .ex5(row_9_ex5), .nb5(row_8_ex21), .ex6(row_9_ex6),
    .nb6(row_8_ex22), .ex7(row_9_ex7), .nb7(row_8_ex23), .ex8(row_9_ex8), .nb8(row_8_ex24), .ex9(row_9_ex9),
    .nb9(row_8_ex25), .ex10(row_9_ex10), .nb10(row_8_ex26), .ex11(row_9_ex11), .nb11(row_8_ex27),
    .ex12(row_9_ex12), .nb12(row_8_ex28), .ex13(row_9_ex13), .nb13(row_8_ex29), .ex14(row_9_ex14),
    .nb14(row_8_ex30), .ex15(row_9_ex15), .nb15(row_8_ex31), .ex16(row_9_ex16), .nb16(row_8_ex32),
    .ex17(row_9_ex17), .nb17(row_10_ex1), .ex18(row_9_ex18), .nb18(row_10_ex2), .ex19(row_9_ex19),
    .nb19(row_10_ex3), .ex20(row_9_ex20), .nb20(row_10_ex4), .ex21(row_9_ex21), .nb21(row_10_ex5),
    .ex22(row_9_ex22), .nb22(row_10_ex6), .ex23(row_9_ex23), .nb23(row_10_ex7), .ex24(row_9_ex24),
    .nb24(row_10_ex8), .ex25(row_9_ex25), .nb25(row_10_ex9), .ex26(row_9_ex26), .nb26(row_10_ex10),
    .ex27(row_9_ex27), .nb27(row_10_ex11), .ex28(row_9_ex28), .nb28(row_10_ex12), .ex29(row_9_ex29),
    .nb29(row_10_ex13), .ex30(row_9_ex30), .nb30(row_10_ex14), .ex31(row_9_ex31), .nb31(row_10_ex15),
    .ex32(row_9_ex32), .nb32(row_10_ex16), .set(set9), .\output (halted_9), .cell_out(out9), .stop(stop),
    .adr(adr));
  row row_10 (
    .clk(clk_t), .ex1(row_10_ex1), .nb1(row_9_ex17), .ex2(row_10_ex2), .nb2(row_9_ex18), .ex3(row_10_ex3),
    .nb3(row_9_ex19), .ex4(row_10_ex4), .nb4(row_9_ex20), .ex5(row_10_ex5), .nb5(row_9_ex21),
    .ex6(row_10_ex6), .nb6(row_9_ex22), .ex7(row_10_ex7), .nb7(row_9_ex23), .ex8(row_10_ex8),
    .nb8(row_9_ex24), .ex9(row_10_ex9), .nb9(row_9_ex25), .ex10(row_10_ex10), .nb10(row_9_ex26),
    .ex11(row_10_ex11), .nb11(row_9_ex27), .ex12(row_10_ex12), .nb12(row_9_ex28), .ex13(row_10_ex13),
    .nb13(row_9_ex29), .ex14(row_10_ex14), .nb14(row_9_ex30), .ex15(row_10_ex15), .nb15(row_9_ex31),
    .ex16(row_10_ex16), .nb16(row_9_ex32), .ex17(row_10_ex17), .nb17(row_11_ex1), .ex18(row_10_ex18),
    .nb18(row_11_ex2), .ex19(row_10_ex19), .nb19(row_11_ex3), .ex20(row_10_ex20), .nb20(row_11_ex4),
    .ex21(row_10_ex21), .nb21(row_11_ex5), .ex22(row_10_ex22), .nb22(row_11_ex6), .ex23(row_10_ex23),
    .nb23(row_11_ex7), .ex24(row_10_ex24), .nb24(row_11_ex8), .ex25(row_10_ex25), .nb25(row_11_ex9),
    .ex26(row_10_ex26), .nb26(row_11_ex10), .ex27(row_10_ex27), .nb27(row_11_ex11), .ex28(row_10_ex28),
    .nb28(row_11_ex12), .ex29(row_10_ex29), .nb29(row_11_ex13), .ex30(row_10_ex30), .nb30(row_11_ex14),
    .ex31(row_10_ex31), .nb31(row_11_ex15), .ex32(row_10_ex32), .nb32(row_11_ex16), .set(set10),
    .\output (halted_10), .cell_out(out10), .stop(stop), .adr(adr));
  row row_11 (
    .clk(clk_t), .ex1(row_11_ex1), .nb1(row_10_ex17), .ex2(row_11_ex2), .nb2(row_10_ex18), .ex3(row_11_ex3),
    .nb3(row_10_ex19), .ex4(row_11_ex4), .nb4(row_10_ex20), .ex5(row_11_ex5), .nb5(row_10_ex21),
    .ex6(row_11_ex6), .nb6(row_10_ex22), .ex7(row_11_ex7), .nb7(row_10_ex23), .ex8(row_11_ex8),
    .nb8(row_10_ex24), .ex9(row_11_ex9), .nb9(row_10_ex25), .ex10(row_11_ex10), .nb10(row_10_ex26),
    .ex11(row_11_ex11), .nb11(row_10_ex27), .ex12(row_11_ex12), .nb12(row_10_ex28), .ex13(row_11_ex13),
    .nb13(row_10_ex29), .ex14(row_11_ex14), .nb14(row_10_ex30), .ex15(row_11_ex15), .nb15(row_10_ex31),
    .ex16(row_11_ex16), .nb16(row_10_ex32), .ex17(row_11_ex17), .nb17(row_12_ex1), .ex18(row_11_ex18),
    .nb18(row_12_ex2), .ex19(row_11_ex19), .nb19(row_12_ex3), .ex20(row_11_ex20), .nb20(row_12_ex4),
    .ex21(row_11_ex21), .nb21(row_12_ex5), .ex22(row_11_ex22), .nb22(row_12_ex6), .ex23(row_11_ex23),
    .nb23(row_12_ex7), .ex24(row_11_ex24), .nb24(row_12_ex8), .ex25(row_11_ex25), .nb25(row_12_ex9),
    .ex26(row_11_ex26), .nb26(row_12_ex10), .ex27(row_11_ex27), .nb27(row_12_ex11), .ex28(row_11_ex28),
    .nb28(row_12_ex12), .ex29(row_11_ex29), .nb29(row_12_ex13), .ex30(row_11_ex30), .nb30(row_12_ex14),
    .ex31(row_11_ex31), .nb31(row_12_ex15), .ex32(row_11_ex32), .nb32(row_12_ex16), .set(set11),
    .\output (halted_11), .cell_out(out11), .stop(stop), .adr(adr));
  row row_12 (
    .clk(clk_t), .ex1(row_12_ex1), .nb1(row_11_ex17), .ex2(row_12_ex2), .nb2(row_11_ex18), .ex3(row_12_ex3),
    .nb3(row_11_ex19), .ex4(row_12_ex4), .nb4(row_11_ex20), .ex5(row_12_ex5), .nb5(row_11_ex21),
    .ex6(row_12_ex6), .nb6(row_11_ex22), .ex7(row_12_ex7), .nb7(row_11_ex23), .ex8(row_12_ex8),
    .nb8(row_11_ex24), .ex9(row_12_ex9), .nb9(row_11_ex25), .ex10(row_12_ex10), .nb10(row_11_ex26),
    .ex11(row_12_ex11), .nb11(row_11_ex27), .ex12(row_12_ex12), .nb12(row_11_ex28), .ex13(row_12_ex13),
    .nb13(row_11_ex29), .ex14(row_12_ex14), .nb14(row_11_ex30), .ex15(row_12_ex15), .nb15(row_11_ex31),
    .ex16(row_12_ex16), .nb16(row_11_ex32), .ex17(row_12_ex17), .nb17(row_13_ex1), .ex18(row_12_ex18),
    .nb18(row_13_ex2), .ex19(row_12_ex19), .nb19(row_13_ex3), .ex20(row_12_ex20), .nb20(row_13_ex4),
    .ex21(row_12_ex21), .nb21(row_13_ex5), .ex22(row_12_ex22), .nb22(row_13_ex6), .ex23(row_12_ex23),
    .nb23(row_13_ex7), .ex24(row_12_ex24), .nb24(row_13_ex8), .ex25(row_12_ex25), .nb25(row_13_ex9),
    .ex26(row_12_ex26), .nb26(row_13_ex10), .ex27(row_12_ex27), .nb27(row_13_ex11), .ex28(row_12_ex28),
    .nb28(row_13_ex12), .ex29(row_12_ex29), .nb29(row_13_ex13), .ex30(row_12_ex30), .nb30(row_13_ex14),
    .ex31(row_12_ex31), .nb31(row_13_ex15), .ex32(row_12_ex32), .nb32(row_13_ex16), .set(set12),
    .\output (halted_12), .cell_out(out12), .stop(stop), .adr(adr));
  row row_13 (
    .clk(clk_t), .ex1(row_13_ex1), .nb1(row_12_ex17), .ex2(row_13_ex2), .nb2(row_12_ex18), .ex3(row_13_ex3),
    .nb3(row_12_ex19), .ex4(row_13_ex4), .nb4(row_12_ex20), .ex5(row_13_ex5), .nb5(row_12_ex21),
    .ex6(row_13_ex6), .nb6(row_12_ex22), .ex7(row_13_ex7), .nb7(row_12_ex23), .ex8(row_13_ex8),
    .nb8(row_12_ex24), .ex9(row_13_ex9), .nb9(row_12_ex25), .ex10(row_13_ex10), .nb10(row_12_ex26),
    .ex11(row_13_ex11), .nb11(row_12_ex27), .ex12(row_13_ex12), .nb12(row_12_ex28), .ex13(row_13_ex13),
    .nb13(row_12_ex29), .ex14(row_13_ex14), .nb14(row_12_ex30), .ex15(row_13_ex15), .nb15(row_12_ex31),
    .ex16(row_13_ex16), .nb16(row_12_ex32), .ex17(row_13_ex17), .nb17(row_14_ex1), .ex18(row_13_ex18),
    .nb18(row_14_ex2), .ex19(row_13_ex19), .nb19(row_14_ex3), .ex20(row_13_ex20), .nb20(row_14_ex4),
    .ex21(row_13_ex21), .nb21(row_14_ex5), .ex22(row_13_ex22), .nb22(row_14_ex6), .ex23(row_13_ex23),
    .nb23(row_14_ex7), .ex24(row_13_ex24), .nb24(row_14_ex8), .ex25(row_13_ex25), .nb25(row_14_ex9),
    .ex26(row_13_ex26), .nb26(row_14_ex10), .ex27(row_13_ex27), .nb27(row_14_ex11), .ex28(row_13_ex28),
    .nb28(row_14_ex12), .ex29(row_13_ex29), .nb29(row_14_ex13), .ex30(row_13_ex30), .nb30(row_14_ex14),
    .ex31(row_13_ex31), .nb31(row_14_ex15), .ex32(row_13_ex32), .nb32(row_14_ex16), .set(set13),
    .\output (halted_13), .cell_out(out13), .stop(stop), .adr(adr));
  row row_14 (
    .clk(clk_t), .ex1(row_14_ex1), .nb1(row_13_ex17), .ex2(row_14_ex2), .nb2(row_13_ex18), .ex3(row_14_ex3),
    .nb3(row_13_ex19), .ex4(row_14_ex4), .nb4(row_13_ex20), .ex5(row_14_ex5), .nb5(row_13_ex21),
    .ex6(row_14_ex6), .nb6(row_13_ex22), .ex7(row_14_ex7), .nb7(row_13_ex23), .ex8(row_14_ex8),
    .nb8(row_13_ex24), .ex9(row_14_ex9), .nb9(row_13_ex25), .ex10(row_14_ex10), .nb10(row_13_ex26),
    .ex11(row_14_ex11), .nb11(row_13_ex27), .ex12(row_14_ex12), .nb12(row_13_ex28), .ex13(row_14_ex13),
    .nb13(row_13_ex29), .ex14(row_14_ex14), .nb14(row_13_ex30), .ex15(row_14_ex15), .nb15(row_13_ex31),
    .ex16(row_14_ex16), .nb16(row_13_ex32), .ex17(row_14_ex17), .nb17(row_15_ex1), .ex18(row_14_ex18),
    .nb18(row_15_ex2), .ex19(row_14_ex19), .nb19(row_15_ex3), .ex20(row_14_ex20), .nb20(row_15_ex4),
    .ex21(row_14_ex21), .nb21(row_15_ex5), .ex22(row_14_ex22), .nb22(row_15_ex6), .ex23(row_14_ex23),
    .nb23(row_15_ex7), .ex24(row_14_ex24), .nb24(row_15_ex8), .ex25(row_14_ex25), .nb25(row_15_ex9),
    .ex26(row_14_ex26), .nb26(row_15_ex10), .ex27(row_14_ex27), .nb27(row_15_ex11), .ex28(row_14_ex28),
    .nb28(row_15_ex12), .ex29(row_14_ex29), .nb29(row_15_ex13), .ex30(row_14_ex30), .nb30(row_15_ex14),
    .ex31(row_14_ex31), .nb31(row_15_ex15), .ex32(row_14_ex32), .nb32(row_15_ex16), .set(set14),
    .\output (halted_14), .cell_out(out14), .stop(stop), .adr(adr));
  row row_15 (
    .clk(clk_t), .ex1(row_15_ex1), .nb1(row_14_ex17), .ex2(row_15_ex2), .nb2(row_14_ex18), .ex3(row_15_ex3),
    .nb3(row_14_ex19), .ex4(row_15_ex4), .nb4(row_14_ex20), .ex5(row_15_ex5), .nb5(row_14_ex21),
    .ex6(row_15_ex6), .nb6(row_14_ex22), .ex7(row_15_ex7), .nb7(row_14_ex23), .ex8(row_15_ex8),
    .nb8(row_14_ex24), .ex9(row_15_ex9), .nb9(row_14_ex25), .ex10(row_15_ex10), .nb10(row_14_ex26),
    .ex11(row_15_ex11), .nb11(row_14_ex27), .ex12(row_15_ex12), .nb12(row_14_ex28), .ex13(row_15_ex13),
    .nb13(row_14_ex29), .ex14(row_15_ex14), .nb14(row_14_ex30), .ex15(row_15_ex15), .nb15(row_14_ex31),
    .ex16(row_15_ex16), .nb16(row_14_ex32), .ex17(row_15_ex17), .nb17(row_16_ex1), .ex18(row_15_ex18),
    .nb18(row_16_ex2), .ex19(row_15_ex19), .nb19(row_16_ex3), .ex20(row_15_ex20), .nb20(row_16_ex4),
    .ex21(row_15_ex21), .nb21(row_16_ex5), .ex22(row_15_ex22), .nb22(row_16_ex6), .ex23(row_15_ex23),
    .nb23(row_16_ex7), .ex24(row_15_ex24), .nb24(row_16_ex8), .ex25(row_15_ex25), .nb25(row_16_ex9),
    .ex26(row_15_ex26), .nb26(row_16_ex10), .ex27(row_15_ex27), .nb27(row_16_ex11), .ex28(row_15_ex28),
    .nb28(row_16_ex12), .ex29(row_15_ex29), .nb29(row_16_ex13), .ex30(row_15_ex30), .nb30(row_16_ex14),
    .ex31(row_15_ex31), .nb31(row_16_ex15), .ex32(row_15_ex32), .nb32(row_16_ex16), .set(set15),
    .\output (halted_15), .cell_out(out15), .stop(stop), .adr(adr));
  row row_16 (
    .clk(clk_t), .ex1(row_16_ex1), .nb1(row_15_ex17), .ex2(row_16_ex2), .nb2(row_15_ex18), .ex3(row_16_ex3),
    .nb3(row_15_ex19), .ex4(row_16_ex4), .nb4(row_15_ex20), .ex5(row_16_ex5), .nb5(row_15_ex21),
    .ex6(row_16_ex6), .nb6(row_15_ex22), .ex7(row_16_ex7), .nb7(row_15_ex23), .ex8(row_16_ex8),
    .nb8(row_15_ex24), .ex9(row_16_ex9), .nb9(row_15_ex25), .ex10(row_16_ex10), .nb10(row_15_ex26),
    .ex11(row_16_ex11), .nb11(row_15_ex27), .ex12(row_16_ex12), .nb12(row_15_ex28), .ex13(row_16_ex13),
    .nb13(row_15_ex29), .ex14(row_16_ex14), .nb14(row_15_ex30), .ex15(row_16_ex15), .nb15(row_15_ex31),
    .ex16(row_16_ex16), .nb16(row_15_ex32), .ex17(tun0), .nb17(tun1), .ex18(tun2), .nb18(tun3), .ex19(tun4),
    .nb19(tun5), .ex20(tun6), .nb20(tun7), .ex21(tun8), .nb21(tun9), .ex22(tun10), .nb22(tun11),
    .ex23(tun12), .nb23(tun13), .ex24(tun14), .nb24(tun15), .ex25(tun16), .nb25(tun17), .ex26(tun18),
    .nb26(tun19), .ex27(tun20), .nb27(tun21), .ex28(tun22), .nb28(tun23), .ex29(tun24), .nb29(tun25),
    .ex30(tun26), .nb30(tun27), .ex31(tun28), .nb31(tun29), .ex32(tun30), .nb32(tun31), .set(set16),
    .\output (halted_16), .cell_out(out16), .stop(stop), .adr(adr));
  Multiplexer #(.select(4), .enable("false")) multiplexer_1 (
    .in0(out1), .in1(out2), .in2(out3), .in3(out4), .in4(out5), .in5(out6), .in6(out7), .in7(out8),
    .in8(out9), .in9(out10), .in10(out11), .in11(out12), .in12(out13), .in13(out14), .in14(out15),
    .in15(out16), .out(cell_out), .sel(adr[7:4]));
  Demultiplexer #(.select(4), .disabled(0)) demultiplexer_1 (
    .out0(set1), .out1(set2), .out2(set3), .out3(set4), .out4(set5), .out5(set6), .out6(set7), .out7(set8),
    .out8(set9), .out9(set10), .out10(set11), .out11(set12), .out12(set13), .out13(set14), .out14(set15),
    .out15(set16), .in(set), .sel(adr[7:4]), .en(set));
  // Probe on adr
  // Probe on adr[7:4]

  // Other names for the same wires on the sheet: adr_4bits[3:0] = adr[7:4]
endmodule

module bcd (
  input  [7:0] \input ,
  output [3:0] big_digit,
  output [3:0] small_digit
);

  wire [3:0] subtractor_1_out;

  Comparator #(.width(4), .mode("unsigned")) comparator_1 (
    .a(\input [3:0]), .b(4'b1010), .eq(big_digit[0]));  // open: gt, lt
  Subtractor #(.width(4)) subtractor_1 (.a(\input [3:0]), .b(4'b1010), .out(subtractor_1_out));  // open: bin, bout
  Multiplexer #(.width(4), .enable("false")) multiplexer_1 (
    .in0(\input [3:0]), .in1(subtractor_1_out), .out(small_digit), .sel(big_digit[0]));

  assign big_digit[3:1] = 3'b000;
endmodule

module cell2 (
  input  ul_nb,
  input  up_nb,
  input  ur_nb,
  input  right_nb,
  input  left_nb,
  input  dr_nb,
  input  dl_nb,
  input  down_nb,
  input  set,
  input  clk,
  input  stop,
  output exit,
  output exit_2
);

  wire and_1_out, and_2_out, and_3_out, and_4_out, multiplexer_1_out, not_1_out, not_2_out, not_3_out,
       not_4_out, or_1_out, or_2_out, t_ff_2_q;
  wire [2:0] adder_1_out, adder_2_out, adder_3_out, adder_4_out, adder_5_out, adder_6_out, adder_7_out,
       xnor_1_out, xnor_2_out;

  Adder #(.width(3)) adder_1 (.a({2'b00, ul_nb}), .b({2'b00, up_nb}), .out(adder_1_out));  // open: cin, cout
  Adder #(.width(3)) adder_2 (.a({2'b00, ur_nb}), .b({2'b00, right_nb}), .out(adder_2_out));  // open: cin, cout
  Adder #(.width(3)) adder_3 (.a({2'b00, left_nb}), .b({2'b00, dr_nb}), .out(adder_3_out));  // open: cin, cout
  Adder #(.width(3)) adder_4 (.a({2'b00, dl_nb}), .b({2'b00, down_nb}), .out(adder_4_out));  // open: cin, cout
  Adder #(.width(3)) adder_5 (.a(adder_1_out), .b(adder_2_out), .out(adder_5_out));  // open: cin, cout
  Adder #(.width(3)) adder_6 (.a(adder_3_out), .b(adder_4_out), .out(adder_6_out));  // open: cin, cout
  not not_1 (not_1_out, exit);
  Adder #(.width(3)) adder_7 (.a(adder_5_out), .b(adder_6_out), .out(adder_7_out));  // open: cin, cout
  and and_1 (and_1_out, exit, not_2_out);
  not not_2 (not_2_out, exit);
  and and_2 (and_2_out, not_1_out, not_3_out);
  not not_3 (not_3_out, not_1_out);
  T_Flip_Flop t_ff_1 (.clk(set), .T(set), .Q(exit));  // open: Qn, preset, reset, en
  T_Flip_Flop t_ff_2 (.clk(set), .T(set), .Q(t_ff_2_q), .reset(or_1_out));  // open: Qn, preset, en
  or or_1 (or_1_out, and_1_out, and_2_out);
  assign xnor_1_out = ~(3'b010 ^ adder_7_out);  // XNOR_Gate xnor_1, 3 bits wide
  and and_3 (and_3_out, xnor_2_out[0], xnor_2_out[1], xnor_2_out[2]);
  assign xnor_2_out = ~(adder_7_out ^ 3'b011);  // XNOR_Gate xnor_2, 3 bits wide
  and and_4 (and_4_out, exit, xnor_1_out[0], xnor_1_out[1], xnor_1_out[2]);
  or or_2 (or_2_out, and_4_out, and_3_out);
  not not_4 (not_4_out, exit);
  Multiplexer #(.enable("false")) multiplexer_1 (
    .in0(or_2_out), .in1(not_4_out), .out(multiplexer_1_out), .sel(t_ff_2_q));

  assign exit_2 = exit;
endmodule
